# Fritzing sketch analog-in (saved by Fritzing 0.9.3b)
breadboards: 1

parts:
  R1 = Resistor [tolerance=±5% resistance=220 package=THT]
  Arduino1 = Arduino Uno (Rev3)
  R2 = Resistor [tolerance=±5% resistance=220 package=THT]
  R3 = Resistor [tolerance=±5% resistance=220 package=THT]
  R4 = Resistor [tolerance=±5% resistance=10k package=THT]
  LED1 = LED - 5mm [color="Red (633nm)" package="5 mm [THT]"]
  LED2 = LED - 5mm [color="Yellow (585nm)" package="5 mm [THT]"]
  LED3 = LED - 5mm [color="Green (555nm)" package="5 mm [THT]"]
  LED4 = LED - 5mm [color="Blue (470nm)" package="5 mm [THT]"]
  U3 = POT [package=3362u]

nets:
  N1: R1.Pin_0, Arduino1.D6_PWM
  N2: R1.Pin_1, LED3.anode
  N3: Arduino1.D4, R3.Pin_0
  N4: Arduino1.D5_PWM, R2.Pin_0
  N5: Arduino1.D7, R4.Pin_0
  N6: Arduino1.5V, U3.A
  N7: Arduino1.GND, LED1.cathode, LED2.cathode, LED3.cathode, LED4.cathode, U3.E
  N8: R2.Pin_1, LED2.anode
  N9: R3.Pin_1, LED1.anode
  N10: R4.Pin_1, LED4.anode
