# Fritzing sketch digital-io (saved by Fritzing 0.9.3b)
breadboards: 1

parts:
  LED1 = LED - 5mm [color="Red (633nm)" package="5 mm [THT]"]
  R1 = Resistor [tolerance=±5% resistance=220 package=THT]
  Arduino1 = Arduino Uno (Rev3)
  S1 = Pushbutton [package="[THT]"]
  R2 = Resistor [tolerance=±5% resistance=10k package=THT]

nets:
  N1: LED1.cathode, R2.Pin_0
  N2: LED1.anode, R1.Pin_1
  N3: R1.Pin_0, Arduino1.D13/SCK
  N4: Arduino1.D2, S1.Pin_3, S1.Pin_4, R2.Pin_1
  N5: S1.Pin_1, S1.Pin_2
