# Fritzing sketch servo (saved by Fritzing 0.9.3b)
breadboards: 1

parts:
  Arduino1 = Arduino Uno (Rev3)
  U3 = POT [package=3362u]
  J1 = Basic Servo
  C1 = Electrolytic Capacitor [capacitance=1µF package="100 mil [THT, electrolytic]"]
  C2 = Electrolytic Capacitor [capacitance=1µF package="100 mil [THT, electrolytic]"]

nets:
  N1: Arduino1.D9_PWM, J1.pulse
  5V: Arduino1.5V, U3.A, J1.vcc, C1.+, C2.+
  GND: Arduino1.GND, U3.E, J1.gnd, C1.-, C2.-
